// Logisim project Computer8Bit.circ as structural Verilog: 16 circuits, main circuit main
module main (
);

  wire and_1_out, clockmodule_1_clk, I0_POLL, I0_TR, I1_POLL, I1_TR, I2_POLL, I2_TR,
       interface_emulator_1_a_out, J, JA, JC, JN, JZ, LCD_EN, LCD_R_NW, LCD_RS, not_1_out, not_2_out,
       not_3_out, not_4_out, not_5_out, not_6_out, not_7_out, NOT_CS_IN, NOT_CS_OUT, NOT_FI, NOT_FLAGS_RS,
       NOT_HLT, NOT_IR_IN, NOT_MAR_IN, NOT_MDS_IN, NOT_PASS, NOT_PC_IN, NOT_PC_INC, NOT_PC_OUT, NOT_RA_IN,
       NOT_RA_OUT, NOT_RA_SL, NOT_RA_SR, NOT_RAM_IN, NOT_RAM_OUT, NOT_RB_IN, NOT_RB_OUT, NOT_RC_IN,
       NOT_RC_OUT, NOT_RD_IN, NOT_RD_OUT, NOT_ROM_OUT, NOT_RT_IN, NOT_RT_OUT, NOT_SAR_IN, NOT_SDS_IN,
       NOT_SP_CT, NOT_SP_IN, NOT_SS_IN, OP_SEL0, OP_SEL1, OP_SEL2, RAM_AS, ROM_AS, SP_DIR, switch_1_p2,
       X_SEL0, X_SEL1, Y_SEL0, Y_SEL1;
  wire [2:0] alu_1_flags;
  wire [3:0] codesegment_programcounter_1_bus_out, codesegment_programcounter_1_bus_out_2,
       flagsregister_1_flags_out;
  wire [6:0] bit_extender_1_out;
  wire [7:0] aluoperandselector_1_o1, aluoperandselector_1_o2, aluoperatorselector_1_op_out,
       bufferedregister_2_async_out, bufferedregister_3_async_out, bufferedregister_4_async_out, IR_q, MAR_q,
       MDS_q, SAR_q, SDS_q, shiftregister_1_async_out, SS_q, stackpointer_1_sp_out, undriven;
  wire [12:0] codesegment_programcounter_1_cs_pc;

  ControlUnit controlunit_1 (
    .IR(IR_q), .CLK(clockmodule_1_clk), .NOT_RA_IN(NOT_RA_IN), .NOT_RA_OUT(NOT_RA_OUT),
    .NOT_RA_SL(NOT_RA_SL), .NOT_RA_SR(NOT_RA_SR), .NOT_RB_IN(NOT_RB_IN), .NOT_RB_OUT(NOT_RB_OUT),
    .NOT_RC_IN(NOT_RC_IN), .NOT_RC_OUT(NOT_RC_OUT), .NOT_RD_IN(NOT_RD_IN), .NOT_RD_OUT(NOT_RD_OUT),
    .NOT_MDS_IN(NOT_MDS_IN), .NOT_MAR_IN(NOT_MAR_IN), .NOT_SS_IN(NOT_SS_IN), .NOT_SP_IN(NOT_SP_IN),
    .NOT_SP_CT(NOT_SP_CT), .SP_DIR(SP_DIR), .NOT_SDS_IN(NOT_SDS_IN), .NOT_SAR_IN(NOT_SAR_IN),
    .NOT_RT_IN(NOT_RT_IN), .NOT_RT_OUT(NOT_RT_OUT), .X_SEL0(X_SEL0), .X_SEL1(X_SEL1), .Y_SEL0(Y_SEL0),
    .Y_SEL1(Y_SEL1), .OP_SEL0(OP_SEL0), .OP_SEL1(OP_SEL1), .OP_SEL2(OP_SEL2), .NOT_RAM_IN(NOT_RAM_IN),
    .NOT_RAM_OUT(NOT_RAM_OUT), .RAM_AS(RAM_AS), .NOT_ROM_OUT(NOT_ROM_OUT), .ROM_AS(ROM_AS),
    .NOT_CS_IN(NOT_CS_IN), .NOT_PC_IN(NOT_PC_IN), .NOT_PC_INC(NOT_PC_INC), .NOT_CS_OUT(NOT_CS_OUT),
    .NOT_PC_OUT(NOT_PC_OUT), .NOT_IR_IN(NOT_IR_IN), .LCD_EN(LCD_EN), .LCD_RS(LCD_RS), .LCD_R_NW(LCD_R_NW),
    .NOT_FI(NOT_FI), .NOT_FLAGS_RS(NOT_FLAGS_RS), .J(J), .JC(JC), .JZ(JZ), .JN(JN), .JA(JA),
    .NOT_PASS(NOT_PASS), .NOT_HLT(NOT_HLT), .I0_POLL(I0_POLL), .I0_TR(I0_TR), .I1_POLL(I1_POLL),
    .I1_TR(I1_TR), .I2_POLL(I2_POLL), .I2_TR(I2_TR));
  LED led_1 (.in(NOT_RA_IN));
  LED led_2 (.in(NOT_RA_OUT));
  LED led_3 (.in(NOT_RA_SL));
  LED led_4 (.in(NOT_RA_SR));
  LED led_5 (.in(NOT_RB_IN));
  LED led_6 (.in(NOT_RB_OUT));
  LED led_7 (.in(NOT_RC_IN));
  LED led_8 (.in(NOT_RC_OUT));
  LED led_9 (.in(NOT_RD_IN));
  LED led_10 (.in(NOT_RD_OUT));
  LED led_11 (.in(NOT_MDS_IN));
  LED led_12 (.in(NOT_MAR_IN));
  LED led_13 (.in(NOT_SS_IN));
  LED led_14 (.in(NOT_SP_IN));
  LED led_15 (.in(NOT_SP_CT));
  LED led_16 (.in(SP_DIR));
  LED led_17 (.in(NOT_SDS_IN));
  LED led_18 (.in(NOT_SAR_IN));
  LED led_19 (.in(NOT_RT_IN));
  LED led_20 (.in(NOT_RT_OUT));
  LED led_21 (.in(X_SEL0));
  LED led_22 (.in(X_SEL1));
  LED led_23 (.in(Y_SEL0));
  LED led_24 (.in(Y_SEL1));
  LED led_25 (.in(OP_SEL0));
  LED led_26 (.in(OP_SEL1));
  LED led_27 (.in(OP_SEL2));
  LED led_28 (.in(NOT_RAM_IN));
  LED led_29 (.in(NOT_RAM_OUT));
  LED led_30 (.in(RAM_AS));
  LED led_31 (.in(NOT_ROM_OUT));
  LED led_32 (.in(ROM_AS));
  LED led_33 (.in(NOT_CS_IN));
  LED led_34 (.in(NOT_PC_IN));
  LED led_35 (.in(NOT_PC_INC));
  LED led_36 (.in(NOT_CS_OUT));
  LED led_37 (.in(NOT_PC_OUT));
  LED led_38 (.in(NOT_IR_IN));
  LED led_39 (.in(LCD_EN));
  LED led_40 (.in(LCD_RS));
  LED led_41 (.in(LCD_R_NW));
  LED led_42 (.in(NOT_FI));
  LED led_43 (.in(NOT_FLAGS_RS));
  LED led_44 (.in(J));
  LED led_45 (.in(JC));
  LED led_46 (.in(JZ));
  LED led_47 (.in(JN));
  LED led_48 (.in(JA));
  LED led_49 (.in(NOT_PASS));
  LED led_50 (.in(NOT_HLT));
  LED led_51 (.in(I0_POLL));
  LED led_52 (.in(I0_TR));
  LED led_53 (.in(I1_POLL));
  LED led_54 (.in(I1_TR));
  LED led_55 (.in(I2_POLL));
  LED led_56 (.in(I2_TR));
  Register SS (
    .D({codesegment_programcounter_1_bus_out_2, codesegment_programcounter_1_bus_out}), .en(not_1_out),
    .clk(clockmodule_1_clk), .Q(SS_q), .clr(1'b0));
  not not_1 (not_1_out, NOT_SS_IN);
  Register MDS (
    .D({codesegment_programcounter_1_bus_out_2, codesegment_programcounter_1_bus_out}), .en(not_2_out),
    .clk(clockmodule_1_clk), .Q(MDS_q), .clr(1'b0));
  not not_2 (not_2_out, NOT_MDS_IN);
  Register SDS (
    .D({codesegment_programcounter_1_bus_out_2, codesegment_programcounter_1_bus_out}), .en(not_3_out),
    .clk(clockmodule_1_clk), .Q(SDS_q));  // open: clr
  not not_3 (not_3_out, NOT_SDS_IN);
  Register MAR (
    .D({codesegment_programcounter_1_bus_out_2, codesegment_programcounter_1_bus_out}), .en(not_4_out),
    .clk(clockmodule_1_clk), .Q(MAR_q), .clr(1'b0));
  not not_4 (not_4_out, NOT_MAR_IN);
  Register SAR (
    .D({codesegment_programcounter_1_bus_out_2, codesegment_programcounter_1_bus_out}), .en(not_5_out),
    .clk(clockmodule_1_clk), .Q(SAR_q));  // open: clr
  not not_5 (not_5_out, NOT_SAR_IN);
  StackPointer stackpointer_1 (
    .NOT_SP_IN(NOT_SP_IN), .SP_DIR(SP_DIR), .NOT_SP_CT(NOT_SP_CT), .CLK(clockmodule_1_clk),
    .SP_OUT(stackpointer_1_sp_out));
  CodeSegment_ProgramCounter codesegment_programcounter_1 (
    .FLAGS(flagsregister_1_flags_out), .J(J), .JC(JC), .JZ(JZ), .JN(JN), .JA(JA), .NOT_PC_IN(NOT_PC_IN),
    .NOT_CS_IN(NOT_CS_IN), .NOT_PC_INC(NOT_PC_INC),
    .BUS_IN({codesegment_programcounter_1_bus_out_2, codesegment_programcounter_1_bus_out}),
    .CLK(clockmodule_1_clk), .NOT_PC_OUT(NOT_PC_OUT), .NOT_CS_OUT(NOT_CS_OUT),
    .CS_PC(codesegment_programcounter_1_cs_pc),
    .BUS_OUT({codesegment_programcounter_1_bus_out_2, codesegment_programcounter_1_bus_out}));
  // DipSwitch dipswitch_1: pin names not known
  // Switch switch_1: pin names not known; wires that end beside it: 1'b1, switch_1_p2
  Pull_Resistor pull_resistor_1 (.node(switch_1_p2));
  assign {codesegment_programcounter_1_bus_out_2, codesegment_programcounter_1_bus_out} = switch_1_p2 ? undriven : 8'bz;  // Controlled_Buffer controlled_buffer_1
  Register IR (
    .D({codesegment_programcounter_1_bus_out_2, codesegment_programcounter_1_bus_out}), .en(not_6_out),
    .clk(clockmodule_1_clk), .Q(IR_q), .clr(1'b0));
  not not_6 (not_6_out, NOT_IR_IN);
  Hex_Digit_Display hex_digit_display_1 (.value(codesegment_programcounter_1_bus_out_2));  // open: dp
  ClockModule clockmodule_1 (.NOT_HLT(NOT_HLT), .CLK(clockmodule_1_clk));
  RAMModule rammodule_1 (
    .BUS_IN({codesegment_programcounter_1_bus_out_2, codesegment_programcounter_1_bus_out}),
    .NOT_RAM_IN(NOT_RAM_IN), .MAR(MAR_q), .SP(stackpointer_1_sp_out), .MDS(MDS_q), .CLK(clockmodule_1_clk),
    .SS(SS_q), .NOT_RAM_OUT(NOT_RAM_OUT), .RAM_AS(RAM_AS),
    .BUS_OUT({codesegment_programcounter_1_bus_out_2, codesegment_programcounter_1_bus_out}));
  ROMModule rommodule_1 (
    .CS_PC(codesegment_programcounter_1_cs_pc), .SAR(SAR_q), .SDS(SDS_q), .ROM_AS(ROM_AS),
    .NOT_ROM_OUT(NOT_ROM_OUT),
    .BUS_OUT({codesegment_programcounter_1_bus_out_2, codesegment_programcounter_1_bus_out}));
  BufferedRegister bufferedregister_1 (
    .BUS_IN({codesegment_programcounter_1_bus_out_2, codesegment_programcounter_1_bus_out}),
    .CLK(clockmodule_1_clk), .NOT_R_IN(NOT_RT_IN), .NOT_R_OUT(NOT_RT_OUT),
    .BUS_OUT({codesegment_programcounter_1_bus_out_2, codesegment_programcounter_1_bus_out}));  // open: ASYNC_OUT
  Hex_Digit_Display hex_digit_display_2 (.value(codesegment_programcounter_1_bus_out));  // open: dp
  not not_7 (not_7_out, LCD_R_NW);
  Bit_Extender #(.out_width(7)) bit_extender_1 (
    .in({codesegment_programcounter_1_bus_out_2, codesegment_programcounter_1_bus_out}),
    .out(bit_extender_1_out));
  TTY #(.cols(16), .rows(2)) tty_1 (.data(bit_extender_1_out), .clk(clockmodule_1_clk), .we(and_1_out));  // open: clr
  and and_1 (and_1_out, not_7_out, LCD_EN);
  BufferedRegister bufferedregister_2 (
    .BUS_IN({codesegment_programcounter_1_bus_out_2, codesegment_programcounter_1_bus_out}),
    .CLK(clockmodule_1_clk), .NOT_R_IN(NOT_RC_IN), .NOT_R_OUT(NOT_RC_OUT),
    .ASYNC_OUT(bufferedregister_2_async_out),
    .BUS_OUT({codesegment_programcounter_1_bus_out_2, codesegment_programcounter_1_bus_out}));
  Hex_Digit_Display hex_digit_display_3 (.value(bufferedregister_2_async_out[7:4]));  // open: dp
  ShiftRegister shiftregister_1 (
    .NOT_SR(NOT_RA_SR), .NOT_IE(NOT_RA_IN), .NOT_SL(NOT_RA_SL), .CLK(clockmodule_1_clk),
    .BUS_IN({codesegment_programcounter_1_bus_out_2, codesegment_programcounter_1_bus_out}),
    .NOT_OE(NOT_RA_OUT), .ASYNC_OUT(shiftregister_1_async_out),
    .BUS_OUT({codesegment_programcounter_1_bus_out_2, codesegment_programcounter_1_bus_out}));
  Hex_Digit_Display hex_digit_display_4 (.value(shiftregister_1_async_out[7:4]));  // open: dp
  Hex_Digit_Display hex_digit_display_5 (.value(bufferedregister_2_async_out[3:0]));  // open: dp
  Hex_Digit_Display hex_digit_display_6 (.value(shiftregister_1_async_out[3:0]));  // open: dp
  ALUOperandSelector aluoperandselector_1 (
    .X_SEL0(X_SEL0), .X_SEL1(X_SEL1), .Y_SEL0(Y_SEL0), .Y_SEL1(Y_SEL1), .A_ASYNC(shiftregister_1_async_out),
    .B_ASYNC(bufferedregister_4_async_out), .C_ASYNC(bufferedregister_2_async_out),
    .D_ASYNC(bufferedregister_3_async_out), .O1(aluoperandselector_1_o1), .O2(aluoperandselector_1_o2));
  Interface_emulator interface_emulator_1 (
    .POLL(I0_POLL), .TRANSMIT(I0_TR), .CLK(clockmodule_1_clk),
    .BUS_IN({codesegment_programcounter_1_bus_out_2, codesegment_programcounter_1_bus_out}),
    .BUS_OUT({codesegment_programcounter_1_bus_out_2, codesegment_programcounter_1_bus_out}),
    .A_OUT(interface_emulator_1_a_out));
  BufferedRegister bufferedregister_3 (
    .BUS_IN({codesegment_programcounter_1_bus_out_2, codesegment_programcounter_1_bus_out}),
    .CLK(clockmodule_1_clk), .NOT_R_IN(NOT_RD_IN), .NOT_R_OUT(NOT_RD_OUT),
    .ASYNC_OUT(bufferedregister_3_async_out),
    .BUS_OUT({codesegment_programcounter_1_bus_out_2, codesegment_programcounter_1_bus_out}));
  BufferedRegister bufferedregister_4 (
    .BUS_IN({codesegment_programcounter_1_bus_out_2, codesegment_programcounter_1_bus_out}),
    .CLK(clockmodule_1_clk), .NOT_R_IN(NOT_RB_IN), .NOT_R_OUT(NOT_RB_OUT),
    .ASYNC_OUT(bufferedregister_4_async_out),
    .BUS_OUT({codesegment_programcounter_1_bus_out_2, codesegment_programcounter_1_bus_out}));
  Hex_Digit_Display hex_digit_display_7 (.value(bufferedregister_4_async_out[7:4]));  // open: dp
  Hex_Digit_Display hex_digit_display_8 (.value(bufferedregister_3_async_out[7:4]));  // open: dp
  Hex_Digit_Display hex_digit_display_9 (.value(bufferedregister_3_async_out[3:0]));  // open: dp
  Hex_Digit_Display hex_digit_display_10 (.value(bufferedregister_4_async_out[3:0]));  // open: dp
  ALUOperatorSelector aluoperatorselector_1 (
    .OP_SEL0(OP_SEL0), .OP_SEL1(OP_SEL1), .OP_SEL2(OP_SEL2), .OP_OUT(aluoperatorselector_1_op_out));
  ALU alu_1 (
    .OPERATORS(aluoperatorselector_1_op_out), .O1(aluoperandselector_1_o1), .O2(aluoperandselector_1_o2),
    .BUS_OUT({codesegment_programcounter_1_bus_out_2, codesegment_programcounter_1_bus_out}),
    .FLAGS(alu_1_flags));
  FLAGSRegister flagsregister_1 (
    .A_IN(interface_emulator_1_a_out), .ALU_FLAGS(alu_1_flags), .CLK(clockmodule_1_clk), .NOT_FI(NOT_FI),
    .FLAGS_OUT(flagsregister_1_flags_out));
  LED led_57 (.in(flagsregister_1_flags_out[3]));
  LED led_58 (.in(flagsregister_1_flags_out[2]));
  LED led_59 (.in(flagsregister_1_flags_out[1]));
  LED led_60 (.in(flagsregister_1_flags_out[0]));

  // Notes on the sheet:
  //   RAM
  //   ROM
  //   Clock
  //   Write to bus
  //   IR
  //   RT
  //   Bus contents
  //   RC
  //   RA
  //   ALU_OPERAND_SELECTOR
  //   RD
  //   RB
  //   ALU_OPERATOR_SELECTOR
  //   A
  //   N
  //   Z
  //   C
endmodule

module ShiftRegister (
  input  NOT_SR,
  input  NOT_IE,
  input  NOT_SL,
  input  CLK,
  input  [7:0] BUS_IN,
  input  NOT_OE,
  output [7:0] ASYNC_OUT,
  output [7:0] BUS_OUT
);

  wire not_1_out, S0_out, S1_out;

  not not_1 (not_1_out, NOT_OE);
  nand S0 (S0_out, NOT_SR, NOT_IE);
  nand S1 (S1_out, NOT_IE, NOT_SL);
  L_8_bit_universal_shift_storage_register_with_3_state_outputs_SN74ALS299_87cfe9f2 l_8_bit_universal_shift_storage_register_with_3_state_outputs_sn74als299_87cfe9f2_1 (
    .BUS_OUT(ASYNC_OUT), .CLK(CLK), .NOT_CLR(1'b1), .NOT_OE1(1'b0), .NOT_OE2(1'b0), .BUS_IN(BUS_IN),
    .S1(S1_out), .SR(1'b0), .S0(S0_out), .SL(1'b0));  // open: QA1, QH1
  assign BUS_OUT = not_1_out ? ASYNC_OUT : 8'bz;  // Controlled_Buffer controlled_buffer_1
endmodule

module BufferedRegister (
  input  [7:0] BUS_IN,
  input  CLK,
  input  NOT_R_IN,
  input  NOT_R_OUT,
  output [7:0] ASYNC_OUT,
  output [7:0] BUS_OUT
);

  wire not_1_out;

  L_3_state_octal_D_flip_flop_74HC574AP_57ace3e5 l_3_state_octal_d_flip_flop_74hc574ap_57ace3e5_1 (
    .Q(ASYNC_OUT), .CLK(CLK), .NOT_DE(NOT_R_IN), .NOT_OE(1'b0), .D(BUS_IN));
  not not_1 (not_1_out, NOT_R_OUT);
  assign BUS_OUT = not_1_out ? ASYNC_OUT : 8'bz;  // Controlled_Buffer controlled_buffer_1
endmodule

module ALUOperandSelector (
  input  X_SEL0,
  input  X_SEL1,
  input  Y_SEL0,
  input  Y_SEL1,
  input  [7:0] A_ASYNC,
  input  [7:0] B_ASYNC,
  input  [7:0] C_ASYNC,
  input  [7:0] D_ASYNC,
  output [7:0] O1,
  output [7:0] O2
);

  wire decoder_1_out0, decoder_1_out1, decoder_1_out2, decoder_1_out3, decoder_2_out0, decoder_2_out1,
       decoder_2_out2, decoder_2_out3;

  Decoder #(.select(2)) decoder_1 (
    .out0(decoder_1_out0), .out1(decoder_1_out1), .out2(decoder_1_out2), .out3(decoder_1_out3),
    .sel({X_SEL1, X_SEL0}), .en(1'b1));
  Decoder #(.select(2)) decoder_2 (
    .out0(decoder_2_out0), .out1(decoder_2_out1), .out2(decoder_2_out2), .out3(decoder_2_out3),
    .sel({Y_SEL1, Y_SEL0}), .en(1'b1));
  assign O1 = decoder_1_out0 ? A_ASYNC : 8'bz;  // Controlled_Buffer controlled_buffer_1
  assign O1 = decoder_1_out1 ? B_ASYNC : 8'bz;  // Controlled_Buffer controlled_buffer_2
  assign O1 = decoder_1_out2 ? C_ASYNC : 8'bz;  // Controlled_Buffer controlled_buffer_3
  assign O1 = decoder_1_out3 ? D_ASYNC : 8'bz;  // Controlled_Buffer controlled_buffer_4
  assign O2 = decoder_2_out0 ? A_ASYNC : 8'bz;  // Controlled_Buffer controlled_buffer_5
  assign O2 = decoder_2_out1 ? B_ASYNC : 8'bz;  // Controlled_Buffer controlled_buffer_6
  assign O2 = decoder_2_out2 ? C_ASYNC : 8'bz;  // Controlled_Buffer controlled_buffer_7
  assign O2 = decoder_2_out3 ? D_ASYNC : 8'bz;  // Controlled_Buffer controlled_buffer_8
endmodule

module ALUOperatorSelector (
  input  OP_SEL0,
  input  OP_SEL1,
  input  OP_SEL2,
  output [7:0] OP_OUT
);

  Decoder #(.select(3)) decoder_1 (
    .out0(OP_OUT[0]), .out1(OP_OUT[1]), .out2(OP_OUT[2]), .out3(OP_OUT[3]), .out4(OP_OUT[4]),
    .out5(OP_OUT[5]), .out6(OP_OUT[6]), .out7(OP_OUT[7]), .sel({OP_SEL2, OP_SEL1, OP_SEL0}), .en(1'b1));
endmodule

module ALU (
  input  [7:0] OPERATORS,
  input  [7:0] O1,
  input  [7:0] O2,
  output [7:0] BUS_OUT,
  output [2:0] FLAGS
);

  wire and_2_out, and_3_out, nor_1_out, nor_2_out, nor_3_out, nor_4_out, or_2_out;
  wire [6:0] buffer_1_out;
  wire [7:0] adder_1_out, and_1_out, bit_extender_1_out, not_1_out, or_1_out, xor_1_out, xor_2_out;

  assign not_1_out = ~O1;  // NOT_Gate not_1, 8 bits wide
  assign xor_1_out = O1 ^ O2;  // XOR_Gate xor_1, 8 bits wide
  assign BUS_OUT = OPERATORS[6] ? not_1_out : 8'bz;  // Controlled_Buffer controlled_buffer_1
  assign BUS_OUT = OPERATORS[5] ? xor_1_out : 8'bz;  // Controlled_Buffer controlled_buffer_2
  assign and_1_out = O1 & O2;  // AND_Gate and_1, 8 bits wide
  assign BUS_OUT = OPERATORS[4] ? and_1_out : 8'bz;  // Controlled_Buffer controlled_buffer_3
  // NoConnect on OPERATORS[7]
  assign or_1_out = O1 | O2;  // OR_Gate or_1, 8 bits wide
  assign BUS_OUT = OPERATORS[3] ? or_1_out : 8'bz;  // Controlled_Buffer controlled_buffer_4
  nor nor_1 (nor_1_out, FLAGS[2], buffer_1_out[6]);
  assign bit_extender_1_out = {{7{OPERATORS[2]}}, OPERATORS[2]};  // Bit_Extender bit_extender_1
  assign {FLAGS[2], buffer_1_out} = BUS_OUT;  // Buffer buffer_1, 8 bits wide
  Pull_Resistor pull_resistor_1 (.node({FLAGS[2], buffer_1_out}));
  nor nor_2 (nor_2_out, buffer_1_out[5], buffer_1_out[4]);
  nor nor_3 (nor_3_out, buffer_1_out[3], buffer_1_out[2]);
  and and_2 (and_2_out, nor_1_out, nor_2_out);
  and and_3 (and_3_out, nor_3_out, nor_4_out);
  and and_4 (FLAGS[1], and_2_out, and_3_out);
  Adder adder_1 (.a(O1), .b(xor_2_out), .out(adder_1_out), .cin(OPERATORS[2]), .cout(FLAGS[0]));
  assign xor_2_out = O2 ^ bit_extender_1_out;  // XOR_Gate xor_2, 8 bits wide
  assign BUS_OUT = or_2_out ? adder_1_out : 8'bz;  // Controlled_Buffer controlled_buffer_5
  nor nor_4 (nor_4_out, buffer_1_out[1], buffer_1_out[0]);
  or or_2 (or_2_out, OPERATORS[2], OPERATORS[1]);
endmodule

module FLAGSRegister (
  input  A_IN,
  input  [2:0] ALU_FLAGS,
  input  CLK,
  input  NOT_FI,
  output [3:0] FLAGS_OUT
);

  wire [7:0] bit_extender_1_out, l_3_state_octal_d_flip_flop_74hc574ap_57ace3e5_1_q;

  assign bit_extender_1_out = {{4{1'b0}}, {A_IN, ALU_FLAGS}};  // Bit_Extender bit_extender_1
  L_3_state_octal_D_flip_flop_74HC574AP_57ace3e5 l_3_state_octal_d_flip_flop_74hc574ap_57ace3e5_1 (
    .Q(l_3_state_octal_d_flip_flop_74hc574ap_57ace3e5_1_q), .CLK(CLK), .NOT_DE(NOT_FI), .NOT_OE(1'b0),
    .D(bit_extender_1_out));
  Bit_Extender #(.out_width(4), .\type ("zero")) bit_extender_2 (
    .in(l_3_state_octal_d_flip_flop_74hc574ap_57ace3e5_1_q), .out(FLAGS_OUT));
endmodule

module ClockModule (
  input  NOT_HLT,
  output CLK
);

  wire clock_1_out;

  Clock clock_1 (.out(clock_1_out));
  and and_1 (CLK, clock_1_out, NOT_HLT);
endmodule

module InstructionRegister (
);

  Counter counter_1 ();  // open: clr, load, up, count, clk, D, carry, Q
endmodule

module RAMModule (
  input  [7:0] BUS_IN,
  input  NOT_RAM_IN,
  input  [7:0] MAR,
  input  [7:0] SP,
  input  [7:0] MDS,
  input  CLK,
  input  [7:0] SS,
  input  NOT_RAM_OUT,
  input  RAM_AS,
  output [7:0] BUS_OUT
);

  wire not_1_out, not_2_out;
  wire [7:0] multiplexer_1_out, multiplexer_2_out, ram_1_data;

  Multiplexer #(.width(8)) multiplexer_1 (.in0(MAR), .in1(SP), .out(multiplexer_1_out), .sel(RAM_AS));
  Multiplexer #(.width(8)) multiplexer_2 (.in0(MDS), .in1(SS), .out(multiplexer_2_out), .sel(RAM_AS));
  RAM #(.addrWidth(13), .asyncread("true"), .databus("bidir")) ram_1 (
    .addr({multiplexer_2_out[4:0], multiplexer_1_out}), .we(not_1_out), .oe(not_2_out), .clk(CLK),
    .data(ram_1_data));
  not not_1 (not_1_out, NOT_RAM_IN);
  assign ram_1_data = not_1_out ? BUS_IN : 8'bz;  // Controlled_Buffer controlled_buffer_1
  not not_2 (not_2_out, NOT_RAM_OUT);
  assign BUS_OUT = not_2_out ? ram_1_data : 8'bz;  // Controlled_Buffer controlled_buffer_2
endmodule

module StackPointer (
  input  NOT_SP_IN,
  input  SP_DIR,
  input  NOT_SP_CT,
  input  CLK,
  output [7:0] SP_OUT
);

  wire not_1_out, not_2_out;

  not not_1 (not_1_out, NOT_SP_IN);
  Counter counter_1 (
    .clr(1'b0), .load(not_1_out), .up(SP_DIR), .count(not_2_out), .clk(CLK), .D({8{1'b0}}), .Q(SP_OUT));  // open: carry
  not not_2 (not_2_out, NOT_SP_CT);
endmodule

module ROMModule (
  input  [12:0] CS_PC,
  input  [7:0] SAR,
  input  [7:0] SDS,
  input  ROM_AS,
  input  NOT_ROM_OUT,
  output [7:0] BUS_OUT
);

  wire not_1_out;
  wire [7:0] STORAGE_ROM_data;
  wire [12:0] multiplexer_1_out;

  Multiplexer #(.width(13)) multiplexer_1 (.in0(CS_PC), .in1({SDS[4:0], SAR}), .out(multiplexer_1_out), .sel(ROM_AS));
  ROM #(.addrWidth(13)) STORAGE_ROM (.addr(multiplexer_1_out), .data(STORAGE_ROM_data));
  assign BUS_OUT = not_1_out ? STORAGE_ROM_data : 8'bz;  // Controlled_Buffer controlled_buffer_1
  not not_1 (not_1_out, NOT_ROM_OUT);

  // Notes on the sheet:
  //   contents of STORAGE_ROM (hex, n*v repeats v):
  //   3b 0 3a 1 b2 6f b5 a b8 4 cb
endmodule

module CodeSegment_ProgramCounter (
  input  [3:0] FLAGS,
  input  J,
  input  JC,
  input  JZ,
  input  JN,
  input  JA,
  input  NOT_PC_IN,
  input  NOT_CS_IN,
  input  NOT_PC_INC,
  input  [7:0] BUS_IN,
  input  CLK,
  input  NOT_PC_OUT,
  input  NOT_CS_OUT,
  output [12:0] CS_PC,
  output [7:0] BUS_OUT
);

  wire and_1_out, and_2_out, and_3_out, and_4_out, nor_1_out, nor_2_out, nor_3_out, not_1_out, not_2_out,
       not_3_out, or_1_out, or_2_out, or_3_out, PC_carry;
  wire [7:5] counter_1_q;

  and and_1 (and_1_out, JC, FLAGS[0]);
  or or_1 (or_1_out, and_1_out, and_2_out);
  and and_2 (and_2_out, JZ, FLAGS[1]);
  and and_3 (and_3_out, JN, FLAGS[2]);
  or or_2 (or_2_out, and_3_out, and_4_out);
  or or_3 (or_3_out, or_1_out, or_2_out);
  nor nor_1 (nor_1_out, J, or_3_out);
  and and_4 (and_4_out, JA, FLAGS[3]);
  nor nor_2 (nor_2_out, NOT_CS_IN, nor_1_out);
  not not_1 (not_1_out, NOT_PC_OUT);
  not not_2 (not_2_out, NOT_CS_OUT);
  Counter counter_1 (
    .clr(counter_1_q[5]), .load(nor_2_out), .up(1'b1), .count(PC_carry), .clk(CLK), .D(BUS_IN),
    .Q({counter_1_q, CS_PC[12:8]}));  // open: carry
  not not_3 (not_3_out, NOT_PC_INC);
  nor nor_3 (nor_3_out, nor_1_out, NOT_PC_IN);
  Counter PC (
    .clr(counter_1_q[5]), .load(nor_3_out), .up(1'b1), .count(not_3_out), .clk(CLK), .D(BUS_IN),
    .carry(PC_carry), .Q(CS_PC[7:0]));
  assign BUS_OUT = not_2_out ? {counter_1_q, CS_PC[12:8]} : 8'bz;  // Controlled_Buffer controlled_buffer_1
  assign BUS_OUT = not_1_out ? CS_PC[7:0] : 8'bz;  // Controlled_Buffer controlled_buffer_2
endmodule

module LCD_emulator (
  input  RS,
  input  R_NW,
  input  LCD_EN,
  input  [7:0] BUS_IN
);
endmodule

module Interface_emulator (
  input  POLL,
  input  TRANSMIT,
  input  CLK,
  input  [7:0] BUS_IN,
  output [7:0] BUS_OUT,
  output A_OUT
);

  wire [7:0] register_1_q;

  Register register_1 (.D(BUS_IN), .en(TRANSMIT), .clk(CLK), .Q(register_1_q));  // open: clr
  assign BUS_OUT = POLL ? register_1_q : 8'bz;  // Controlled_Buffer controlled_buffer_1

  assign A_OUT = POLL;
endmodule

module ControlUnit (
  input  [7:0] IR,
  input  CLK,
  output NOT_RA_IN,
  output NOT_RA_OUT,
  output NOT_RA_SL,
  output NOT_RA_SR,
  output NOT_RB_IN,
  output NOT_RB_OUT,
  output NOT_RC_IN,
  output NOT_RC_OUT,
  output NOT_RD_IN,
  output NOT_RD_OUT,
  output NOT_MDS_IN,
  output NOT_MAR_IN,
  output NOT_SS_IN,
  output NOT_SP_IN,
  output NOT_SP_CT,
  output SP_DIR,
  output NOT_SDS_IN,
  output NOT_SAR_IN,
  output NOT_RT_IN,
  output NOT_RT_OUT,
  output X_SEL0,
  output X_SEL1,
  output Y_SEL0,
  output Y_SEL1,
  output OP_SEL0,
  output OP_SEL1,
  output OP_SEL2,
  output NOT_RAM_IN,
  output NOT_RAM_OUT,
  output RAM_AS,
  output NOT_ROM_OUT,
  output ROM_AS,
  output NOT_CS_IN,
  output NOT_PC_IN,
  output NOT_PC_INC,
  output NOT_CS_OUT,
  output NOT_PC_OUT,
  output NOT_IR_IN,
  output LCD_EN,
  output LCD_RS,
  output LCD_R_NW,
  output NOT_FI,
  output NOT_FLAGS_RS,
  output J,
  output JC,
  output JZ,
  output JN,
  output JA,
  output NOT_PASS,
  output NOT_HLT,
  output I0_POLL,
  output I0_TR,
  output I1_POLL,
  output I1_TR,
  output I2_POLL,
  output I2_TR
);

  wire not_1_out, not_2_out;
  wire [3:0] counter_1_q;

  not not_1 (not_1_out, NOT_PASS);
  not not_2 (not_2_out, CLK);
  Counter #(.max('hf), .width(4)) counter_1 (
    .clr(not_1_out), .load(1'b0), .up(1'b1), .count(1'b1), .clk(not_2_out), .D(4'b1111), .Q(counter_1_q));  // open: carry
  ROM #(.addrWidth(13)) EEPROM0 (
    .addr({1'b0, IR, counter_1_q}),
    .data({NOT_RC_OUT, NOT_RC_IN, NOT_RB_OUT, NOT_RB_IN, NOT_RA_SR, NOT_RA_SL, NOT_RA_OUT, NOT_RA_IN}));
  ROM #(.addrWidth(13)) EEPROM1 (
    .addr({1'b0, IR, counter_1_q}),
    .data({SP_DIR, NOT_SP_CT, NOT_SP_IN, NOT_SS_IN, NOT_MAR_IN, NOT_MDS_IN, NOT_RD_OUT, NOT_RD_IN}));
  ROM #(.addrWidth(13)) EEPROM2 (
    .addr({1'b0, IR, counter_1_q}),
    .data({Y_SEL1, Y_SEL0, X_SEL1, X_SEL0, NOT_RT_OUT, NOT_RT_IN, NOT_SAR_IN, NOT_SDS_IN}));
  ROM #(.addrWidth(13)) EEPROM3 (
    .addr({1'b0, IR, counter_1_q}),
    .data({ROM_AS, NOT_ROM_OUT, RAM_AS, NOT_RAM_OUT, NOT_RAM_IN, OP_SEL2, OP_SEL1, OP_SEL0}));
  ROM #(.addrWidth(13)) EEPROM4 (
    .addr({1'b0, IR, counter_1_q}),
    .data({LCD_RS, LCD_EN, NOT_IR_IN, NOT_PC_OUT, NOT_CS_OUT, NOT_PC_INC, NOT_PC_IN, NOT_CS_IN}));
  ROM #(.addrWidth(13)) EEPROM5 (
    .addr({1'b0, IR, counter_1_q}), .data({JA, JN, JZ, JC, J, NOT_FLAGS_RS, NOT_FI, LCD_R_NW}));
  ROM #(.addrWidth(13)) EEPROM6 (
    .addr({1'b0, IR, counter_1_q}), .data({I2_TR, I2_POLL, I1_TR, I1_POLL, I0_TR, I0_POLL, NOT_HLT, NOT_PASS}));

  // Notes on the sheet:
  //   contents of EEPROM0 (hex, n*v repeats v):
  //   34*ff ed 15*ff bd 15*ff fd 15*ff de 15*ff 9f 15*ff df 15*ff 7e 15*ff 6f 15*ff 7f 15*ff fe 15*ff ef
  //   15*ff bf 79*ff df fd 14*ff 7f fd 15*ff fd 14*ff fd df 14*ff 7f df 15*ff df 14*ff fd 7f 14*ff df 7f
  //   15*ff 7f 14*ff fd 15*ff df 15*ff 7f 16*ff fd 15*ff df 15*ff 7f 31*ff fe 15*ff ef 15*ff bf 31*ff fe
  //   15*ff ef 15*ff bf 30*ff fd fe 14*ff fd ef 14*ff fd bf 14*ff fd 15*ff df fe 14*ff df fe 14*ff df bf
  //   14*ff df 15*ff 7f fe 14*ff 7f ef 14*ff 7f ef 14*ff 7f 16*ff fe 15*ff ef 15*ff bf 15*ff bf 14*ff fe
  //   15*ff ef 15*ff bf 127*ff fd 15*ff df 15*ff 7f 64*ff fe 15*ff ef 15*ff bf 31*ff fe 15*ff fe 15*ff fe
  //   15*ff fe 14*ff ef 15*ff ef 15*ff ef 15*ff ef 15*ff bf 15*ff bf 15*ff bf 15*ff bf 80*ff fe 15*ff fe
  //   15*ff fe 15*ff fe 14*ff ef 15*ff ef 15*ff ef 15*ff ef 15*ff bf 15*ff bf 15*ff bf 15*ff bf 336*ff fe
  //   15*ff fe 15*ff fe 15*ff fe 14*ff ef 15*ff ef 15*ff ef 15*ff ef 15*ff bf 15*ff bf 15*ff bf 15*ff bf
  //   80*ff fe 15*ff fe 15*ff fe 15*ff fe 14*ff ef 15*ff ef 15*ff ef 15*ff ef 15*ff bf 15*ff bf 15*ff bf
  //   15*ff bf 80*ff fe 15*ff fe 15*ff fe 15*ff fe 14*ff ef 15*ff ef 15*ff ef 15*ff ef 15*ff bf 15*ff bf
  //   15*ff bf 15*ff bf 80*ff fe 14*ff ef 15*ff bf 31*ff fb 15*ff f7 207*ff fe 15*ff ef 15*ff bf 31*ff fd
  //   15*ff df 15*ff 7f 63*ff fe 15*ff ef 15*ff bf 31*ff fd 15*ff df 15*ff 7f 63*ff fe 15*ff ef 15*ff bf
  //   31*ff fd 15*ff df 15*ff 7f 77*ff
  //   contents of EEPROM1 (hex, n*v repeats v):
  //   66*7f 7e 47*7f 7e 47*7f 7e 15*7f 7d 15*7f 7d 15*7f 7d 15*7f 6d 15*7f 79 15*7f 7d 15*7f 5d 15*7f 77
  //   15*7f 77 15*7f 75 15*7f 77 15*7f 77 15*7f 75 15*7f 77 15*7f 77 15*7f 75 15*7f 77 7d 14*7f 77 7d
  //   14*7f 77 7d 14*7f 77 15*7f 77 15*7f 77 15*7f 77 7d 63*7f 7e 14*7f 77 15*7f 77 15*7f 77 15*7f 77 7e
  //   14*7f 77 15*7f 77 15*7f 77 15*7f 77 7e 14*7f 77 15*7f 77 15*7f 77 15*7f 77 7e 14*7f 77 15*7f 77
  //   15*7f 77 15*7f 77 7e 14*7f 75 15*7f 75 15*7f 75 15*7f 75 63*7f 7e 15*7f 6f 15*7f 7b 31*7f 5f 33*7f
  //   77 14*7f bf 15*7f bf 15*7f bf 14*7f 7d bf 15*7f bf 16*7f bf 13*7f 3f 15*7f 3f 15*7f 3f 15*7f 3f 7e
  //   206*7f 7e 15*7f 7e 15*7f 7e 15*7f 7e 207*7f 7e 15*7f 7e 15*7f 7e 15*7f 7e 463*7f 7e 15*7f 7e 15*7f
  //   7e 15*7f 7e 207*7f 7e 15*7f 7e 15*7f 7e 15*7f 7e 207*7f 7e 15*7f 7e 15*7f 7e 15*7f 7e 63*7f 7e
  //   208*7f bf 7f bf 12*7f 3f 7f 3f 61*7f 7e 63*7f 7d 15*7f 77 79*7f 7e 63*7f 7d 15*7f 77 79*7f 7e 63*7f
  //   7d 15*7f 77 45*7f
  //   contents of EEPROM2 (hex, n*v repeats v):
  //   258*f e 287*f d 15*f d 15*f d 15*f d 431*f e 47*f d 95*f d 79*f b 7 14*f 4b 7 14*f 8b 7 14*f cb 7
  //   14*f 1f 15*f 5f 15*f 9f 15*f df 15*f 2f 15*f 6f 15*f af 15*f ef 15*f 3f 15*f 7f 15*f bf 15*f ff 15*f
  //   b 7 14*f 4b 7 14*f 8b 7 14*f cb 7 14*f 1f 15*f 5f 15*f 9f 15*f df 15*f 2f 15*f 6f 15*f af 15*f ef
  //   15*f 3f 15*f 7f 15*f bf 15*f ff 31*f 4f 15*f 8f 15*f cf 15*f 1f 15*f 5f 15*f 9f 15*f df 15*f 2f 15*f
  //   6f 15*f af 15*f ef 15*f 3f 15*f 7f 15*f bf 15*f ff 15*f b 7 14*f 4b 7 14*f 8b 7 14*f cb 7 14*f 1f
  //   15*f 5f 15*f 9f 15*f df 15*f 2f 15*f 6f 15*f af 15*f ef 15*f 3f 15*f 7f 15*f bf 15*f ff 15*f b 7
  //   14*f 4b 7 14*f 8b 7 14*f cb 7 14*f 1f 15*f 5f 15*f 9f 15*f df 15*f 2f 15*f 6f 15*f af 15*f ef 15*f
  //   3f 15*f 7f 15*f bf 15*f ff 15*f b 7 14*f 4b 7 14*f 8b 7 14*f cb 7 14*f 1f 15*f 5f 15*f 9f 15*f df
  //   15*f 2f 15*f 6f 15*f af 15*f ef 15*f 3f 15*f 7f 15*f bf 15*f ff 15*f b 7 14*f 1f 15*f 2f 15*f 3f
  //   47*f b f 7 13*f b f 7 13*f b f 7 13*f b f 7 29*f b f f 7 12*f b f f 7 12*f b f f 7 12*f b f f 7 12*f
  //   b f f 7 15*f b f f 7 169*f d 159*f d 159*f d 29*f
  //   contents of EEPROM3 (hex, n*v repeats v):
  //   18 15*58 18 15*58 18 15*58 18 15*58 18 15*58 18 15*58 18 15*58 18 15*58 18 15*58 18 15*58 18 15*58
  //   18 15*58 18 15*58 18 15*58 18 15*58 18 15*58 18 15*58 18 15*58 18 58 58 50 12*58 18 58 58 50 12*58
  //   18 58 58 50 12*58 18 58 58 50 12*58 18 58 58 50 12*58 18 58 58 50 12*58 18 58 58 50 12*58 18 58 58
  //   50 12*58 18 58 58 50 12*58 18 58 58 50 12*58 18 58 58 50 12*58 18 58 58 50 12*58 18 58 18 50 12*58
  //   18 58 18 50 12*58 18 58 18 50 12*58 18 58 18 50 12*58 18 58 18 98 12*58 18 58 18 98 12*58 18 58 18
  //   98 12*58 18 58 18 98 12*58 18 58 18 48 12*58 18 58 18 48 12*58 18 58 18 48 12*58 18 58 18 48 12*58
  //   18 58 58 48 12*58 18 58 58 48 12*58 18 58 58 48 12*58 18 58 58 48 12*58 18 58 58 48 12*58 18 58 58
  //   48 12*58 18 58 58 48 12*58 18 58 58 48 12*58 18 58 58 48 12*58 18 58 58 48 12*58 18 58 58 48 12*58
  //   18 58 58 48 12*58 18 58 58 48 12*58 18 58 58 48 12*58 18 58 58 48 12*58 18 58 58 48 12*58 18 58 18
  //   13*58 18 58 18 13*58 18 58 18 13*58 18 58 18 13*58 18 58 18 13*58 18 58 18 13*58 18 58 18 13*58 18
  //   58 18 13*58 18 58 10 13*58 18 58 18 58 18 90 10*58 18 58 70 13*58 18 58 70 13*58 18 58 70 13*58 18
  //   58 70 13*58 18 58 30 13*58 18 58 18 b0 12*58 18 58 58 68 12*58 18 58 58 68 12*58 18 58 58 68 12*58
  //   18 58 58 68 12*58 18 58 59 13*58 18 58 59 13*58 18 58 59 13*58 18 58 59 13*58 18 58 59 13*58 18 58
  //   59 13*58 18 58 59 13*58 18 58 59 13*58 18 58 59 13*58 18 58 59 13*58 18 58 59 13*58 18 58 59 13*58
  //   18 58 59 13*58 18 58 59 13*58 18 58 59 13*58 18 58 59 13*58 18 58 5a 13*58 18 58 5a 13*58 18 58 5a
  //   13*58 18 58 5a 13*58 18 58 5a 13*58 18 58 5a 13*58 18 58 5a 13*58 18 58 5a 13*58 18 58 5a 13*58 18
  //   58 5a 13*58 18 58 5a 13*58 18 58 5a 13*58 18 58 5a 13*58 18 58 5a 13*58 18 58 5a 13*58 18 58 5a
  //   13*58 18 58 5a 13*58 18 58 5a 13*58 18 58 5a 13*58 18 58 5a 13*58 18 58 5a 13*58 18 58 5a 13*58 18
  //   58 5a 13*58 18 58 5a 13*58 18 58 5a 13*58 18 58 5a 13*58 18 58 5a 13*58 18 58 5a 13*58 18 58 5a
  //   13*58 18 58 5a 13*58 18 58 5a 13*58 18 58 5a 13*58 18 58 5b 13*58 18 58 5b 13*58 18 58 5b 13*58 18
  //   58 5b 13*58 18 58 5b 13*58 18 58 5b 13*58 18 58 5b 13*58 18 58 5b 13*58 18 58 5b 13*58 18 58 5b
  //   13*58 18 58 5b 13*58 18 58 5b 13*58 18 58 5b 13*58 18 58 5b 13*58 18 58 5b 13*58 18 58 5b 13*58 18
  //   58 5c 13*58 18 58 5c 13*58 18 58 5c 13*58 18 58 5c 13*58 18 58 5c 13*58 18 58 5c 13*58 18 58 5c
  //   13*58 18 58 5c 13*58 18 58 5c 13*58 18 58 5c 13*58 18 58 5c 13*58 18 58 5c 13*58 18 58 5c 13*58 18
  //   58 5c 13*58 18 58 5c 13*58 18 58 5c 13*58 18 58 5d 13*58 18 58 5d 13*58 18 58 5d 13*58 18 58 5d
  //   13*58 18 58 5d 13*58 18 58 5d 13*58 18 58 5d 13*58 18 58 5d 13*58 18 58 5d 13*58 18 58 5d 13*58 18
  //   58 5d 13*58 18 58 5d 13*58 18 58 5d 13*58 18 58 5d 13*58 18 58 5d 13*58 18 58 5d 13*58 18 58 5e
  //   13*58 18 58 5e 13*58 18 58 5e 13*58 18 58 5e 13*58 18 15*58 18 15*58 18 58 18 13*58 18 58 18 13*58
  //   18 58 18 13*58 18 58 18 13*58 18 58 18 13*58 18 58 18 58 18 11*58 18 58 18 58 18 11*58 18 58 18 58
  //   18 11*58 18 58 18 58 18 11*58 18 58 18 58 18 11*58 18 58 70 58 70 18 58 18 8*58 18 58 58 68 58 68
  //   10*58 18 15*58 18 15*58 18 15*58 18 15*58 18 15*58 18 15*58 18 15*58 18 15*58 18 58 18 13*58 18 58
  //   18 98 12*58 18 15*58 18 15*58 18 15*58 18 15*58 18 15*58 18 15*58 18 15*58 18 15*58 18 58 18 13*58
  //   18 58 18 98 12*58 18 15*58 18 15*58 18 15*58 18 15*58 18 15*58 18 15*58 18 15*58 18 15*58 18 58 18
  //   13*58 18 58 18 98 12*58 18 15*58
  //   contents of EEPROM4 (hex, n*v repeats v):
  //   1f 3b 14*3f 1f 3b 14*3f 1f 3b 14*3f 1f 3b 14*3f 1f 3b 14*3f 1f 3b 14*3f 1f 3b 14*3f 1f 3b 14*3f 1f
  //   3b 14*3f 1f 3b 14*3f 1f 3b 14*3f 1f 3b 14*3f 1f 3b 14*3f 1f 3b 14*3f 1f 3b 14*3f 1f 3b 14*3f 1f 3b
  //   14*3f 1f 3b 14*3f 1f 3b 14*3f 1f 3b 14*3f 1f 3b 14*3f 1f 3b 14*3f 1f 3b 14*3f 1f 3b 14*3f 1f 3b
  //   14*3f 1f 3b 14*3f 1f 3b 14*3f 1f 3b 14*3f 1f 3b 14*3f 1f 3b 14*3f 1f 3b 3f 3b 12*3f 1f 3b 3f 3b
  //   12*3f 1f 3b 3f 3b 12*3f 1f 3b 3f 3b 12*3f 1f 3b 3f 3b 12*3f 1f 3b 3f 3b 12*3f 1f 3b 3f 3b 12*3f 1f
  //   3b 3f 3b 12*3f 1f 3b 3f 3b 12*3f 1f 3b 3f 3b 12*3f 1f 3b 3f 3b 12*3f 1f 3b 3f 3b 12*3f 1f 3b 14*3f
  //   1f 3b 14*3f 1f 3b 14*3f 1f 3b 14*3f 1f 3b 14*3f 1f 3b 14*3f 1f 3b 14*3f 1f 3b 14*3f 1f 3b 14*3f 1f
  //   3b 14*3f 1f 3b 14*3f 1f 3b 14*3f 1f 3b 14*3f 1f 3b 14*3f 1f 3b 14*3f 1f 3b 14*3f 1f 3b 3f 3b 12*3f
  //   1f 3b 3f 3b 12*3f 1f 3b 3f 3b 12*3f 1f 3b 3f 3b 12*3f 1f 3b 3f 3b 12*3f 1f 3b 3f 3b 12*3f 1f 3b 3f
  //   3b 12*3f 1f 3b 3f 3b 12*3f 1f 3b 3f 3b 12*3f 1f 3b 3f 3b 3f 3b 10*3f 1f 3b 14*3f 1f 3b 14*3f 1f 3b
  //   14*3f 1f 3b 14*3f 1f 3b 3f 3b 12*3f 1f 3b 3f 3b 12*3f 1f 3b 14*3f 1f 3b 14*3f 1f 3b 14*3f 1f 3b
  //   14*3f 1f 3b 14*3f 1f 3b 14*3f 1f 3b 14*3f 1f 3b 14*3f 1f 3b 14*3f 1f 3b 14*3f 1f 3b 14*3f 1f 3b
  //   14*3f 1f 3b 14*3f 1f 3b 14*3f 1f 3b 14*3f 1f 3b 14*3f 1f 3b 14*3f 1f 3b 14*3f 1f 3b 14*3f 1f 3b
  //   14*3f 1f 3b 14*3f 1f 3b 14*3f 1f 3b 14*3f 1f 3b 14*3f 1f 3b 14*3f 1f 3b 14*3f 1f 3b 14*3f 1f 3b
  //   14*3f 1f 3b 14*3f 1f 3b 14*3f 1f 3b 14*3f 1f 3b 14*3f 1f 3b 14*3f 1f 3b 14*3f 1f 3b 14*3f 1f 3b
  //   14*3f 1f 3b 14*3f 1f 3b 14*3f 1f 3b 14*3f 1f 3b 14*3f 1f 3b 14*3f 1f 3b 14*3f 1f 3b 14*3f 1f 3b
  //   14*3f 1f 3b 14*3f 1f 3b 14*3f 1f 3b 14*3f 1f 3b 14*3f 1f 3b 14*3f 1f 3b 14*3f 1f 3b 14*3f 1f 3b
  //   14*3f 1f 3b 14*3f 1f 3b 14*3f 1f 3b 14*3f 1f 3b 14*3f 1f 3b 14*3f 1f 3b 14*3f 1f 3b 14*3f 1f 3b
  //   14*3f 1f 3b 14*3f 1f 3b 14*3f 1f 3b 14*3f 1f 3b 14*3f 1f 3b 14*3f 1f 3b 14*3f 1f 3b 14*3f 1f 3b
  //   14*3f 1f 3b 14*3f 1f 3b 14*3f 1f 3b 14*3f 1f 3b 14*3f 1f 3b 14*3f 1f 3b 14*3f 1f 3b 14*3f 1f 3b
  //   14*3f 1f 3b 14*3f 1f 3b 14*3f 1f 3b 14*3f 1f 3b 14*3f 1f 3b 14*3f 1f 3b 14*3f 1f 3b 14*3f 1f 3b
  //   14*3f 1f 3b 14*3f 1f 3b 14*3f 1f 3b 14*3f 1f 3b 14*3f 1f 3b 14*3f 1f 3b 14*3f 1f 3b 14*3f 1f 3b
  //   14*3f 1f 3b 14*3f 1f 3b 14*3f 1f 3b 14*3f 1f 3b 14*3f 1f 3b 14*3f 1f 3b 14*3f 1f 3b 14*3f 1f 3b
  //   14*3f 1f 3b 14*3f 1f 3b 14*3f 1f 3b 14*3f 1f 3b 14*3f 1f 3b 14*3f 1f 3b 14*3f 1f 3b 3f 3b 3d 11*3f
  //   1f 3b 3f 3b 3d 11*3f 1f 3b 3f 3b 3d 11*3f 1f 3b 3f 3b 3d 11*3f 1f 3b 3d 13*3f 1f 3b 3f 3b 3d 3e
  //   10*3f 1f 3b 3f 3b 3d 3e 10*3f 1f 3b 3f 3b 3d 3e 10*3f 1f 3b 3f 3b 3d 3e 10*3f 1f 3b 3f 3b 3d 3e
  //   10*3f 1f 3b 37 3f 2f 3f 3b 3d 3e 7*3f 1f 3b 3f 3d 3b 3a 10*3f 1f 3b 14*3f 1f 3b 14*3f 1f 3b 14*3f 1f
  //   3b 14*3f 1f 3b 14*3f 1f 3b 14*3f 1f 3b 14*3f 1f 3b 14*3f 1f 3b 3f 3b 12*3f 1f 3b 3f 3b 12*3f 1f 3b
  //   14*3f 1f 3b 14*3f 1f 3b 14*3f 1f 3b 14*3f 1f 3b 14*3f 1f 3b 14*3f 1f 3b 14*3f 1f 3b 14*3f 1f 3b 3f
  //   3b 12*3f 1f 3b 3f 3b 12*3f 1f 3b 14*3f 1f 3b 14*3f 1f 3b 14*3f 1f 3b 14*3f 1f 3b 14*3f 1f 3b 14*3f
  //   1f 3b 14*3f 1f 3b 14*3f 1f 3b 3f 3b 12*3f 1f 3b 3f 3b 12*3f 1f 3b 14*3f
  //   contents of EEPROM5 (hex, n*v repeats v):
  //   1250*6 4 15*6 4 15*6 4 15*6 4 15*6 4 15*6 4 15*6 4 15*6 4 15*6 4 15*6 4 15*6 4 15*6 4 15*6 4 15*6 4
  //   15*6 4 15*6 4 15*6 4 15*6 4 15*6 4 15*6 4 15*6 4 15*6 4 15*6 4 15*6 4 15*6 4 15*6 4 15*6 4 15*6 4
  //   15*6 4 15*6 4 15*6 4 15*6 4 15*6 4 15*6 4 15*6 4 15*6 4 15*6 4 15*6 4 15*6 4 15*6 4 15*6 4 15*6 4
  //   15*6 4 15*6 4 15*6 4 15*6 4 15*6 4 15*6 4 15*6 4 15*6 4 15*6 4 15*6 4 15*6 4 15*6 4 15*6 4 15*6 4
  //   15*6 4 15*6 4 15*6 4 15*6 4 15*6 4 15*6 4 15*6 4 15*6 4 15*6 4 15*6 4 15*6 4 15*6 4 15*6 4 15*6 4
  //   15*6 4 15*6 4 15*6 4 15*6 4 15*6 4 15*6 4 15*6 4 15*6 4 15*6 4 15*6 4 15*6 4 15*6 4 15*6 4 15*6 4
  //   15*6 4 15*6 4 15*6 4 15*6 4 15*6 4 15*6 4 15*6 4 15*6 4 15*6 4 15*6 4 15*6 4 15*6 4 15*6 4 15*6 4
  //   15*6 4 15*6 4 49*6 16 15*6 26 15*6 46 15*6 86 13*6 e 17*6 16 16 14*6 26 26 14*6 46 46 14*6 86 86
  //   14*6 e e 17*6 e e 10*6 e 6 e 12*6 4 15*6 4 15*6 4 15*6 4 111*6 4 15*6 4 15*6 4 15*6 4 111*6 4 15*6 4
  //   15*6 4 15*6 4 111*6 2 13*6
  //   contents of EEPROM6 (hex, n*v repeats v):
  //   3 3 1 2 14*3 2 16*3 2 15*3 2 15*3 2 15*3 2 15*3 2 15*3 2 15*3 2 15*3 2 15*3 2 15*3 2 15*3 2 15*3 2
  //   15*3 2 15*3 2 15*3 2 15*3 2 16*3 2 15*3 2 15*3 2 15*3 2 15*3 2 15*3 2 15*3 2 15*3 2 15*3 2 15*3 2
  //   15*3 2 15*3 2 15*3 2 15*3 2 15*3 2 15*3 2 15*3 2 15*3 2 15*3 2 15*3 2 15*3 2 15*3 2 15*3 2 15*3 2
  //   15*3 2 15*3 2 15*3 2 15*3 2 15*3 2 15*3 2 15*3 2 15*3 2 15*3 2 15*3 2 15*3 2 15*3 2 15*3 2 15*3 2
  //   15*3 2 15*3 2 15*3 2 15*3 2 15*3 2 15*3 2 15*3 2 15*3 2 15*3 2 15*3 2 15*3 2 17*3 2 13*3 2 15*3 2
  //   15*3 2 15*3 2 15*3 2 16*3 2 14*3 2 15*3 2 15*3 2 15*3 2 15*3 2 15*3 2 15*3 2 15*3 2 14*3 2 15*3 2
  //   15*3 2 15*3 2 15*3 2 15*3 2 15*3 2 15*3 2 15*3 2 15*3 2 15*3 2 15*3 2 16*3 2 15*3 2 15*3 2 15*3 2
  //   14*3 2 15*3 2 15*3 2 15*3 2 15*3 2 15*3 2 15*3 2 15*3 2 15*3 2 15*3 2 15*3 2 15*3 2 15*3 2 15*3 2
  //   15*3 2 15*3 2 15*3 2 15*3 2 15*3 2 15*3 2 15*3 2 15*3 2 15*3 2 15*3 2 15*3 2 15*3 2 15*3 2 15*3 2
  //   16*3 2 15*3 2 15*3 2 15*3 2 14*3 2 15*3 2 15*3 2 15*3 2 15*3 2 15*3 2 15*3 2 15*3 2 15*3 2 15*3 2
  //   15*3 2 15*3 2 16*3 2 15*3 2 15*3 2 15*3 2 14*3 2 15*3 2 15*3 2 15*3 2 15*3 2 15*3 2 15*3 2 15*3 2
  //   15*3 2 15*3 2 15*3 2 15*3 2 16*3 2 15*3 2 15*3 2 15*3 2 14*3 2 15*3 2 15*3 2 15*3 2 15*3 2 15*3 2
  //   15*3 2 15*3 2 15*3 2 15*3 2 15*3 2 15*3 2 16*3 2 14*3 2 15*3 2 15*3 2 15*3 2 15*3 2 17*3 2 15*3 2
  //   15*3 2 15*3 2 13*3 2 18*3 2 15*3 2 15*3 2 15*3 2 15*3 2 18*3 2 12*3 2 11*3 7 2 14*3 7 2 14*3 7 2
  //   14*3 7 2 14*3 b 2 14*3 b 2 14*3 b 2 14*3 b 2 15*3 b 2 14*3 b 2 13*3 13 2 14*3 13 2 14*3 13 2 14*3 13
  //   2 14*3 23 2 14*3 23 2 14*3 23 2 14*3 23 2 15*3 23 2 14*3 23 2 13*3 43 2 14*3 43 2 14*3 43 2 14*3 43
  //   2 14*3 83 2 14*3 83 2 14*3 83 2 14*3 83 2 15*3 83 2 14*3 83 2 14*3 2 12*3
endmodule
